// Logisim project controlunit.circ as structural Verilog: 1 circuit, main circuit control unit
module control_unit (
  input  [3:0] opcode,
  output RegDst,
  output Jump,
  output Branch,
  output BNE,
  output MemRead,
  output MemtoReg,
  output MemWrite,
  output ALUSrc,
  output RegWrite,
  output [2:0] ALUOp
);

  and R_type (ALUOp[2], ~opcode[3], ~opcode[2], ~opcode[1], ~opcode[0]);  // AND_Gate
  and lw (MemRead, ~opcode[3], ~opcode[2], ~opcode[1], opcode[0]);  // AND_Gate
  and sw (MemWrite, ~opcode[3], ~opcode[2], opcode[1], ~opcode[0]);  // AND_Gate
  and beq (Branch, ~opcode[3], ~opcode[2], opcode[1], opcode[0]);  // AND_Gate
  or or_1 (ALUOp[0], MemWrite, MemRead);
  and u_bne (BNE, ~opcode[3], opcode[2], ~opcode[1], ~opcode[0]);  // AND_Gate
  or or_2 (ALUOp[1], BNE, Branch);
  and u_jump (Jump, ~opcode[3], opcode[2], opcode[1], opcode[0]);  // AND_Gate
  or or_3 (ALUSrc, MemWrite, MemRead);
  or or_4 (RegWrite, MemRead, ALUOp[2]);

  assign MemtoReg = MemRead;
  assign RegDst = ALUOp[2];
endmodule
